// Logisim project Circuit.circ as structural Verilog: 9 circuits, main circuit main
module main (
);

  wire clock_1_out, cpu_1_port_0_read, cpu_1_port_0_set, cpu_1_ram_set;
  wire [6:0] bit_extender_2_out, keyboard_1_data;
  wire [23:0] cpu_1_ip_out, cpu_1_ram_ptr_out;
  wire [31:0] bit_extender_1_out, cpu_1_io_out, cpu_1_xout, RVM_RAM_dout;
  wire [63:0] RVM_ROM_data;

  Clock clock_1 (.out(clock_1_out));
  Keyboard keyboard_1 (.clk(clock_1_out), .re(cpu_1_port_0_read), .data(keyboard_1_data));  // open: clr, avail
  ROM #(.addrWidth(24), .dataWidth(64)) RVM_ROM (.addr(cpu_1_ip_out), .data(RVM_ROM_data));
  assign bit_extender_1_out = {{25{1'b0}}, keyboard_1_data};  // Bit_Extender bit_extender_1
  CPU cpu_1 (
    .instruction(RVM_ROM_data), .RAM(RVM_RAM_dout), .clock(clock_1_out), .port_0(bit_extender_1_out),
    .Xout(cpu_1_xout), .RAM_set(cpu_1_ram_set), .RAM_ptr_out(cpu_1_ram_ptr_out), .IP_out(cpu_1_ip_out),
    .IO_out(cpu_1_io_out), .port_0_set(cpu_1_port_0_set), .port_0_read(cpu_1_port_0_read));  // open: port_1, port_2, port_3, port_4, port_5, port_6, port_7, port_1_set, port_2_set, port_3_set, port_4_set, port_5_set, port_6_set, port_7_set, port_1_read, port_2_read, port_3_read, port_4_read, port_5_read, port_6_read, port_7_read
  Bit_Extender #(.in_width(32), .out_width(7), .\type ("zero")) bit_extender_2 (
    .in(cpu_1_io_out), .out(bit_extender_2_out));
  RAM #(.addrWidth(24), .dataWidth(32)) RVM_RAM (
    .addr(cpu_1_ram_ptr_out), .we(cpu_1_ram_set), .oe(1'b1), .clk(clock_1_out), .din(cpu_1_xout),
    .dout(RVM_RAM_dout));
  TTY tty_1 (.data(bit_extender_2_out), .clk(clock_1_out), .we(cpu_1_port_0_set));  // open: clr

  // Notes on the sheet:
  //   contents of RVM_ROM (hex, n*v repeats v):
  //   800200d0 800400d0 8000f0d0
endmodule

module arithmetic_unit (
  input  op2,
  input  op1,
  input  op0,
  input  [31:0] X,
  input  [31:0] Y,
  output [2:0] flags,
  output [31:0] Xout
);

  wire [4:0] bit_extender_1_out;
  wire [31:0] adder_1_out, divider_1_out, multiplier_1_out, negator_1_out, shifter_1_out, shifter_2_out,
       subtractor_1_out;

  Adder #(.width(32)) adder_1 (.a(X), .b(Y), .out(adder_1_out));  // open: cin, cout
  Subtractor #(.width(32)) subtractor_1 (.a(X), .b(Y), .out(subtractor_1_out));  // open: bin, bout
  Multiplier #(.width(32)) multiplier_1 (.a(X), .b(Y), .out(multiplier_1_out));  // open: cin, cout
  Divider #(.width(32)) divider_1 (.a(X), .b(Y), .out(divider_1_out));  // open: upper, rem
  Bit_Extender #(.in_width(32), .out_width(5), .\type ("zero")) bit_extender_1 (.in(Y), .out(bit_extender_1_out));
  Negator #(.width(32)) negator_1 (.in(X), .out(negator_1_out));
  Shifter #(.width(32)) shifter_1 (.in(X), .\dist (bit_extender_1_out), .out(shifter_1_out));
  Shifter #(.shift("lr"), .width(32)) shifter_2 (.in(X), .\dist (bit_extender_1_out), .out(shifter_2_out));
  Multiplexer #(.select(3), .width(32)) multiplexer_1 (
    .in0(X), .in1(adder_1_out), .in2(subtractor_1_out), .in3(multiplier_1_out), .in4(divider_1_out),
    .in5(negator_1_out), .in6(shifter_1_out), .in7(shifter_2_out), .out(Xout), .sel({op2, op1, op0}));
  Comparator #(.width(32)) comparator_1 (.a(X), .b(Y), .gt(flags[2]), .eq(flags[1]), .lt(flags[0]));
endmodule

module logical_unit (
  input  op2,
  input  op1,
  input  op0,
  input  [31:0] X,
  input  [31:0] Y,
  output [31:0] Xout
);

  wire [31:0] and_1_out, nand_1_out, nor_1_out, not_1_out, or_1_out, xnor_1_out, xor_1_out;

  assign and_1_out = X & Y;  // AND_Gate and_1, 32 bits wide
  assign or_1_out = X | Y;  // OR_Gate or_1, 32 bits wide
  assign nand_1_out = ~(X & Y);  // NAND_Gate nand_1, 32 bits wide
  assign nor_1_out = ~(X | Y);  // NOR_Gate nor_1, 32 bits wide
  assign not_1_out = ~X;  // NOT_Gate not_1, 32 bits wide
  assign xor_1_out = X ^ Y;  // XOR_Gate xor_1, 32 bits wide
  Multiplexer #(.select(3), .width(32)) multiplexer_1 (
    .in0(X), .in1(and_1_out), .in2(or_1_out), .in3(nand_1_out), .in4(nor_1_out), .in5(not_1_out),
    .in6(xor_1_out), .in7(xnor_1_out), .out(Xout), .sel({op2, op1, op0}));
  assign xnor_1_out = ~(X ^ Y);  // XNOR_Gate xnor_1, 32 bits wide
endmodule

module ALU (
  input  op3,
  input  op2,
  input  op1,
  input  op0,
  input  [31:0] X,
  input  [31:0] Y,
  output [2:0] flags,
  output [31:0] Xout
);

  wire [2:0] arithmetic_unit_1_flags, bit_extender_1_out, not_1_out;
  wire [31:0] arithmetic_unit_1_xout, logical_unit_1_xout;

  assign bit_extender_1_out = {{2{1'b0}}, op3};  // Bit_Extender bit_extender_1
  assign not_1_out = ~bit_extender_1_out;  // NOT_Gate not_1, 3 bits wide
  arithmetic_unit arithmetic_unit_1 (
    .op2(op2), .op1(op1), .op0(op0), .X(X), .Y(Y), .flags(arithmetic_unit_1_flags),
    .Xout(arithmetic_unit_1_xout));
  logical_unit logical_unit_1 (.op2(op2), .op1(op1), .op0(op0), .X(X), .Y(Y), .Xout(logical_unit_1_xout));
  assign flags = not_1_out & arithmetic_unit_1_flags;  // AND_Gate and_1, 3 bits wide
  Multiplexer #(.width(32)) multiplexer_1 (
    .in0(arithmetic_unit_1_xout), .in1(logical_unit_1_xout), .out(Xout), .sel(op3));
endmodule

module ALU_instruction (
  input  [31:0] instruction,
  input  [31:0] A,
  input  [31:0] B,
  input  [31:0] C,
  input  [31:0] D,
  input  [31:0] E,
  input  [31:0] F,
  input  [31:0] G,
  input  [31:0] H,
  input  [31:0] SP,
  input  [31:0] IP,
  input  [31:0] RAM_ptr,
  input  [31:0] RAM,
  input  [31:0] IO,
  input  [31:0] X,
  output [2:0] flags,
  output [31:0] Xout,
  output A_set,
  output B_set,
  output C_set,
  output D_set,
  output E_set,
  output F_set,
  output G_set,
  output H_set,
  output SP_set,
  output IP_set,
  output RAM_ptr_set,
  output RAM_set,
  output IO_set
);

  wire [31:0] multiplexer_1_out, multiplexer_2_out;

  Multiplexer #(.select(4), .width(32)) multiplexer_1 (
    .in0(A), .in1(B), .in2(C), .in3(D), .in4(E), .in5(F), .in6(G), .in7(H), .in8(SP), .in9(IP),
    .in10(RAM_ptr), .in11(RAM), .in12(IO), .out(multiplexer_1_out), .sel(instruction[11:8]));  // open: in13, in14, in15
  Multiplexer #(.select(4), .width(32)) multiplexer_2 (
    .in0(A), .in1(B), .in2(C), .in3(D), .in4(E), .in5(F), .in6(G), .in7(H), .in8(SP), .in9(IP),
    .in10(RAM_ptr), .in11(RAM), .in12(IO), .in13(X), .out(multiplexer_2_out), .sel(instruction[7:4]));  // open: in14, in15
  ALU alu_1 (
    .op3(instruction[3]), .op2(instruction[2]), .op1(instruction[1]), .op0(instruction[0]),
    .X(multiplexer_1_out), .Y(multiplexer_2_out), .flags(flags), .Xout(Xout));
  Demultiplexer #(.select(4)) demultiplexer_1 (
    .out0(A_set), .out1(B_set), .out2(C_set), .out3(D_set), .out4(E_set), .out5(F_set), .out6(G_set),
    .out7(H_set), .out8(SP_set), .out9(IP_set), .out10(RAM_ptr_set), .out11(RAM_set), .out12(IO_set),
    .in(instruction[31]), .sel(instruction[11:8]));  // open: out13, out14, out15
endmodule

module non_ALU_instruction (
  input  [2:0] flags,
  input  [31:0] instruction,
  input  [31:0] A,
  input  [31:0] B,
  input  [31:0] C,
  input  [31:0] D,
  input  [31:0] E,
  input  [31:0] F,
  input  [31:0] G,
  input  [31:0] H,
  input  [31:0] SP,
  input  [31:0] IP,
  input  [31:0] RAM_ptr,
  input  [31:0] RAM,
  input  [31:0] IO,
  input  [31:0] X,
  output [31:0] Xout,
  output A_set,
  output B_set,
  output C_set,
  output D_set,
  output E_set,
  output F_set,
  output G_set,
  output H_set,
  output SP_set,
  output IP_set,
  output RAM_ptr_set,
  output RAM_set,
  output IO_set
);

  wire and_1_out, and_2_out, and_3_out, and_4_out, and_5_out, demultiplexer_1_out12, or_1_out;

  Multiplexer #(.select(4), .width(32)) multiplexer_1 (
    .in0(A), .in1(B), .in2(C), .in3(D), .in4(E), .in5(F), .in6(G), .in7(H), .in8(SP), .in9(IP),
    .in10(RAM_ptr), .in11(RAM), .in12(IO), .in13(X), .out(Xout), .sel(instruction[7:4]));  // open: in14, in15
  and and_1 (and_1_out, flags[0], instruction[12]);
  and and_2 (and_2_out, flags[1], instruction[13]);
  and and_3 (and_3_out, flags[2], instruction[14]);
  or or_1 (or_1_out, and_1_out, and_2_out, and_3_out);
  Demultiplexer #(.select(4)) demultiplexer_1 (
    .out0(A_set), .out1(B_set), .out2(C_set), .out3(D_set), .out4(E_set), .out5(F_set), .out6(G_set),
    .out7(H_set), .out8(SP_set), .out10(RAM_ptr_set), .out11(RAM_set), .out12(demultiplexer_1_out12),
    .in(instruction[16]), .sel(instruction[11:8]));  // open: out9, out13, out14, out15
  and and_4 (and_4_out, instruction[12], instruction[13], instruction[14]);
  and and_5 (and_5_out, or_1_out, instruction[15]);
  or or_2 (IP_set, and_5_out, and_4_out);
  or or_3 (IO_set, demultiplexer_1_out12, instruction[17]);
endmodule

module control_unit (
  input  [2:0] flags,
  input  [31:0] instruction,
  input  [31:0] A,
  input  [31:0] B,
  input  [31:0] C,
  input  [31:0] D,
  input  [31:0] E,
  input  [31:0] F,
  input  [31:0] G,
  input  [31:0] H,
  input  [31:0] SP,
  input  [31:0] IP,
  input  [31:0] RAM_ptr,
  input  [31:0] RAM,
  input  [31:0] IO,
  input  [31:0] X,
  output flags_set,
  output [2:0] flags_out,
  output [31:0] Xout,
  output A_set,
  output B_set,
  output C_set,
  output D_set,
  output E_set,
  output F_set,
  output G_set,
  output H_set,
  output SP_set,
  output IP_set,
  output RAM_ptr_set,
  output RAM_set,
  output IO_set
);

  wire alu_instruction_1_a_set, alu_instruction_1_b_set, alu_instruction_1_c_set, alu_instruction_1_d_set,
       alu_instruction_1_e_set, alu_instruction_1_f_set, alu_instruction_1_g_set, alu_instruction_1_h_set,
       alu_instruction_1_io_set, alu_instruction_1_ip_set, alu_instruction_1_ram_ptr_set,
       alu_instruction_1_ram_set, alu_instruction_1_sp_set, non_alu_instruction_1_a_set,
       non_alu_instruction_1_b_set, non_alu_instruction_1_c_set, non_alu_instruction_1_d_set,
       non_alu_instruction_1_e_set, non_alu_instruction_1_f_set, non_alu_instruction_1_g_set,
       non_alu_instruction_1_h_set, non_alu_instruction_1_io_set, non_alu_instruction_1_ip_set,
       non_alu_instruction_1_ram_ptr_set, non_alu_instruction_1_ram_set, non_alu_instruction_1_sp_set;
  wire [31:0] alu_instruction_1_xout, non_alu_instruction_1_xout;

  not not_1 (flags_set, instruction[31]);
  ALU_instruction alu_instruction_1 (
    .instruction(instruction), .A(A), .B(B), .C(C), .D(D), .E(E), .F(F), .G(G), .H(H), .SP(SP), .IP(IP),
    .RAM_ptr(RAM_ptr), .RAM(RAM), .IO(IO), .X(X), .flags(flags_out), .Xout(alu_instruction_1_xout),
    .A_set(alu_instruction_1_a_set), .B_set(alu_instruction_1_b_set), .C_set(alu_instruction_1_c_set),
    .D_set(alu_instruction_1_d_set), .E_set(alu_instruction_1_e_set), .F_set(alu_instruction_1_f_set),
    .G_set(alu_instruction_1_g_set), .H_set(alu_instruction_1_h_set), .SP_set(alu_instruction_1_sp_set),
    .IP_set(alu_instruction_1_ip_set), .RAM_ptr_set(alu_instruction_1_ram_ptr_set),
    .RAM_set(alu_instruction_1_ram_set), .IO_set(alu_instruction_1_io_set));
  non_ALU_instruction non_alu_instruction_1 (
    .flags(flags), .instruction(instruction), .A(A), .B(B), .C(C), .D(D), .E(E), .F(F), .G(G), .H(H),
    .SP(SP), .IP(IP), .RAM_ptr(RAM_ptr), .RAM(RAM), .IO(IO), .X(X), .Xout(non_alu_instruction_1_xout),
    .A_set(non_alu_instruction_1_a_set), .B_set(non_alu_instruction_1_b_set),
    .C_set(non_alu_instruction_1_c_set), .D_set(non_alu_instruction_1_d_set),
    .E_set(non_alu_instruction_1_e_set), .F_set(non_alu_instruction_1_f_set),
    .G_set(non_alu_instruction_1_g_set), .H_set(non_alu_instruction_1_h_set),
    .SP_set(non_alu_instruction_1_sp_set), .IP_set(non_alu_instruction_1_ip_set),
    .RAM_ptr_set(non_alu_instruction_1_ram_ptr_set), .RAM_set(non_alu_instruction_1_ram_set),
    .IO_set(non_alu_instruction_1_io_set));
  Multiplexer multiplexer_1 (
    .in0(alu_instruction_1_a_set), .in1(non_alu_instruction_1_a_set), .out(A_set), .sel(instruction[31]));
  Multiplexer multiplexer_2 (
    .in0(alu_instruction_1_b_set), .in1(non_alu_instruction_1_b_set), .out(B_set), .sel(instruction[31]));
  Multiplexer multiplexer_3 (
    .in0(alu_instruction_1_c_set), .in1(non_alu_instruction_1_c_set), .out(C_set), .sel(instruction[31]));
  Multiplexer multiplexer_4 (
    .in0(alu_instruction_1_d_set), .in1(non_alu_instruction_1_d_set), .out(D_set), .sel(instruction[31]));
  Multiplexer multiplexer_5 (
    .in0(alu_instruction_1_e_set), .in1(non_alu_instruction_1_e_set), .out(E_set), .sel(instruction[31]));
  Multiplexer multiplexer_6 (
    .in0(alu_instruction_1_f_set), .in1(non_alu_instruction_1_f_set), .out(F_set), .sel(instruction[31]));
  Multiplexer multiplexer_7 (
    .in0(alu_instruction_1_g_set), .in1(non_alu_instruction_1_g_set), .out(G_set), .sel(instruction[31]));
  Multiplexer multiplexer_8 (
    .in0(alu_instruction_1_h_set), .in1(non_alu_instruction_1_h_set), .out(H_set), .sel(instruction[31]));
  Multiplexer multiplexer_9 (
    .in0(alu_instruction_1_sp_set), .in1(non_alu_instruction_1_sp_set), .out(SP_set), .sel(instruction[31]));
  Multiplexer multiplexer_10 (
    .in0(alu_instruction_1_ip_set), .in1(non_alu_instruction_1_ip_set), .out(IP_set), .sel(instruction[31]));
  Multiplexer multiplexer_11 (
    .in0(alu_instruction_1_ram_ptr_set), .in1(non_alu_instruction_1_ram_ptr_set), .out(RAM_ptr_set),
    .sel(instruction[31]));
  Multiplexer multiplexer_12 (
    .in0(alu_instruction_1_ram_set), .in1(non_alu_instruction_1_ram_set), .out(RAM_set), .sel(instruction[31]));
  Multiplexer multiplexer_13 (
    .in0(alu_instruction_1_io_set), .in1(non_alu_instruction_1_io_set), .out(IO_set), .sel(instruction[31]));
  Multiplexer #(.width(32)) multiplexer_14 (
    .in0(alu_instruction_1_xout), .in1(non_alu_instruction_1_xout), .out(Xout), .sel(instruction[31]));
endmodule

module CPU (
  input  [63:0] instruction,
  input  [31:0] RAM,
  input  clock,
  input  [31:0] port_0,
  input  [31:0] port_1,
  input  [31:0] port_2,
  input  [31:0] port_3,
  input  [31:0] port_4,
  input  [31:0] port_5,
  input  [31:0] port_6,
  input  [31:0] port_7,
  output [31:0] Xout,
  output RAM_set,
  output [23:0] RAM_ptr_out,
  output [23:0] IP_out,
  output [31:0] IO_out,
  output port_0_set,
  output port_1_set,
  output port_2_set,
  output port_3_set,
  output port_4_set,
  output port_5_set,
  output port_6_set,
  output port_7_set,
  output port_0_read,
  output port_1_read,
  output port_2_read,
  output port_3_read,
  output port_4_read,
  output port_5_read,
  output port_6_read,
  output port_7_read
);

  wire control_unit_1_a_set, control_unit_1_b_set, control_unit_1_c_set, control_unit_1_d_set,
       control_unit_1_e_set, control_unit_1_f_set, control_unit_1_flags_set, control_unit_1_g_set,
       control_unit_1_h_set, control_unit_1_io_set, control_unit_1_ip_set, control_unit_1_ram_ptr_set,
       control_unit_1_sp_set, io_chip_1_io_set, multiplexer_2_out;
  wire [2:0] bit_extender_6_out, control_unit_1_flags_out, flags_q;
  wire [31:0] A_q, B_q, C_q, D_q, E_q, F_q, G_q, H_q, IO_q, IP_q, multiplexer_1_out, RAM_ptr_q, SP_q;

  Register #(.width(32)) A (.D(Xout), .en(control_unit_1_a_set), .clk(clock), .Q(A_q));  // open: clr
  Register #(.width(32)) C (.D(Xout), .en(control_unit_1_c_set), .clk(clock), .Q(C_q));  // open: clr
  Register #(.width(32)) E (.D(Xout), .en(control_unit_1_e_set), .clk(clock), .Q(E_q));  // open: clr
  Register #(.width(32)) G (.D(Xout), .en(control_unit_1_g_set), .clk(clock), .Q(G_q));  // open: clr
  Register #(.width(32)) SP (.D(Xout), .en(control_unit_1_sp_set), .clk(clock), .Q(SP_q));  // open: clr
  Register #(.width(3)) flags (
    .D(control_unit_1_flags_out), .en(control_unit_1_flags_set), .clk(clock), .Q(flags_q));  // open: clr
  Register #(.width(32)) B (.D(Xout), .en(control_unit_1_b_set), .clk(clock), .Q(B_q));  // open: clr
  Register #(.width(32)) D (.D(Xout), .en(control_unit_1_d_set), .clk(clock), .Q(D_q));  // open: clr
  Register #(.width(32)) F (.D(Xout), .en(control_unit_1_f_set), .clk(clock), .Q(F_q));  // open: clr
  Register #(.width(32)) H (.D(Xout), .en(control_unit_1_h_set), .clk(clock), .Q(H_q));  // open: clr
  Register #(.width(32)) RAM_ptr (.D(Xout), .en(control_unit_1_ram_ptr_set), .clk(clock), .Q(RAM_ptr_q));  // open: clr
  Counter #(.max('hffffffff), .width(32)) IP (
    .load(control_unit_1_ip_set), .up(1'b1), .count(1'b1), .clk(clock), .D(Xout), .Q(IP_q));  // open: clr, carry
  Bit_Extender #(.in_width(7), .out_width(32), .\type ("zero")) bit_extender_1 ();  // open: in, out
  Bit_Extender #(.in_width(7), .out_width(32), .\type ("zero")) bit_extender_2 ();  // open: in, out
  Bit_Extender #(.in_width(7), .out_width(32), .\type ("zero")) bit_extender_3 ();  // open: in, out
  Bit_Extender #(.in_width(32), .out_width(24), .\type ("zero")) bit_extender_4 (.in(RAM_ptr_q), .out(RAM_ptr_out));
  Multiplexer #(.width(32)) multiplexer_1 (.in0(Xout), .in1(IO_out), .out(multiplexer_1_out), .sel(instruction[17]));
  Bit_Extender #(.in_width(32), .out_width(24), .\type ("zero")) bit_extender_5 (.in(IP_q), .out(IP_out));
  Register #(.width(32)) IO (.D(multiplexer_1_out), .en(multiplexer_2_out), .clk(clock), .Q(IO_q));  // open: clr
  Multiplexer multiplexer_2 (
    .in0(control_unit_1_io_set), .in1(io_chip_1_io_set), .out(multiplexer_2_out), .sel(instruction[17]));
  control_unit control_unit_1 (
    .flags(flags_q), .instruction(instruction[31:0]), .A(A_q), .B(B_q), .C(C_q), .D(D_q), .E(E_q), .F(F_q),
    .G(G_q), .H(H_q), .SP(SP_q), .IP(IP_q), .RAM_ptr(RAM_ptr_q), .RAM(RAM), .IO(IO_q),
    .X(instruction[63:32]), .flags_set(control_unit_1_flags_set), .flags_out(control_unit_1_flags_out),
    .Xout(Xout), .A_set(control_unit_1_a_set), .B_set(control_unit_1_b_set), .C_set(control_unit_1_c_set),
    .D_set(control_unit_1_d_set), .E_set(control_unit_1_e_set), .F_set(control_unit_1_f_set),
    .G_set(control_unit_1_g_set), .H_set(control_unit_1_h_set), .SP_set(control_unit_1_sp_set),
    .IP_set(control_unit_1_ip_set), .RAM_ptr_set(control_unit_1_ram_ptr_set), .RAM_set(RAM_set),
    .IO_set(control_unit_1_io_set));
  Bit_Extender #(.in_width(32), .out_width(3), .\type ("zero")) bit_extender_6 (.in(Xout), .out(bit_extender_6_out));
  IO_chip io_chip_1 (
    .read(instruction[17]), .write(instruction[18]), .port_number(bit_extender_6_out), .IO(IO_q),
    .port_0(port_0), .port_1(port_1), .port_2(port_2), .port_3(port_3), .port_4(port_4), .port_5(port_5),
    .port_6(port_6), .port_7(port_7), .IO_set(io_chip_1_io_set), .IO_out(IO_out), .port_0_set(port_0_set),
    .port_1_set(port_1_set), .port_2_set(port_2_set), .port_3_set(port_3_set), .port_4_set(port_4_set),
    .port_5_set(port_5_set), .port_6_set(port_6_set), .port_7_set(port_7_set), .port_0_read(port_0_read),
    .port_1_read(port_1_read), .port_2_read(port_2_read), .port_3_read(port_3_read),
    .port_4_read(port_4_read), .port_5_read(port_5_read), .port_6_read(port_6_read), .port_7_read(port_7_read));
endmodule

module IO_chip (
  input  read,
  input  write,
  input  [2:0] port_number,
  input  [31:0] IO,
  input  [31:0] port_0,
  input  [31:0] port_1,
  input  [31:0] port_2,
  input  [31:0] port_3,
  input  [31:0] port_4,
  input  [31:0] port_5,
  input  [31:0] port_6,
  input  [31:0] port_7,
  output IO_set,
  output [31:0] IO_out,
  output port_0_set,
  output port_1_set,
  output port_2_set,
  output port_3_set,
  output port_4_set,
  output port_5_set,
  output port_6_set,
  output port_7_set,
  output port_0_read,
  output port_1_read,
  output port_2_read,
  output port_3_read,
  output port_4_read,
  output port_5_read,
  output port_6_read,
  output port_7_read
);

  wire and_1_out, not_1_out;
  wire [31:0] multiplexer_1_out;

  Multiplexer #(.select(3), .width(32)) multiplexer_1 (
    .in0(port_0), .in1(port_1), .in2(port_2), .in3(port_3), .in4(port_4), .in5(port_5), .in6(port_6),
    .in7(port_7), .out(multiplexer_1_out), .sel(port_number));
  not not_1 (not_1_out, read);
  and and_1 (and_1_out, not_1_out, write);
  Multiplexer #(.width(32)) multiplexer_2 (.in0(multiplexer_1_out), .in1(IO), .out(IO_out), .sel(and_1_out));
  Demultiplexer #(.select(3)) demultiplexer_1 (
    .out0(port_0_set), .out1(port_1_set), .out2(port_2_set), .out3(port_3_set), .out4(port_4_set),
    .out5(port_5_set), .out6(port_6_set), .out7(port_7_set), .in(write), .sel(port_number));
  Demultiplexer #(.select(3)) demultiplexer_2 (
    .out0(port_0_read), .out1(port_1_read), .out2(port_2_read), .out3(port_3_read), .out4(port_4_read),
    .out5(port_5_read), .out6(port_6_read), .out7(port_7_read), .in(read), .sel(port_number));

  assign IO_set = read;
endmodule
